# Fritzing sketch Stompbox Veroboard (saved by Fritzing 0.9.3b)
stripboards: 1
breadboards: 1

parts:
  U1 = OP482 - Low Power, High Speed JFET Quad Operational Amplifier [part_number=MPC6004]
  R2 = Resistor [tolerance=±5% resistance=1k package="0805 [SMD]"]
  R3 = Resistor [tolerance=±5% resistance=3.9k package="0805 [SMD]"]
  C1 = Ceramic Capacitor [capacitance="100 nF" voltage=16V package="1206 [SMD, multilayer]"]
  C2 = Electrolytic Capacitor [capacitance=22µF voltage=16V package="0807 [SMD, electrolytic]"]
  R5 = Resistor [tolerance=±5% resistance=1M package="0805 [SMD]"]
  R7 = Resistor [tolerance=±5% resistance=24k package="0805 [SMD]"]
  R8 = Resistor [tolerance=±5% resistance=75k package="0805 [SMD]"]
  C3 = Ceramic Capacitor [capacitance="100 nF" voltage=16V package="1206 [SMD, multilayer]"]
  C4 = Ceramic Capacitor [capacitance=1nF voltage=16V part_number=820p package="1206 [SMD, multilayer]"]
  R9 = Resistor [tolerance=±5% resistance=75k package="0805 [SMD]"]
  C5 = Ceramic Capacitor [capacitance=0.1nF voltage=16V package="200 mil [THT, multilayer]"]
  C6 = Ceramic Capacitor [capacitance=1nF voltage=16V part_number=3n9 package="1206 [SMD, multilayer]"]
  R11 = Resistor [tolerance=±5% resistance=3.9k package="0805 [SMD]"]
  C7 = Ceramic Capacitor [capacitance=0.1nF voltage=16V package="200 mil [THT, multilayer]"]
  R12 = Resistor [tolerance=±5% resistance=75k package="0805 [SMD]"]
  R13 = Resistor [tolerance=±5% resistance=36k package="0805 [SMD]"]
  C8 = Ceramic Capacitor [capacitance=1nF voltage=16V part_number=1n2 package="1206 [SMD, multilayer]"]
  R14 = Resistor [tolerance=±5% resistance=75k package="0805 [SMD]"]
  R15 = Resistor [tolerance=±5% resistance=3.9k package="0805 [SMD]"]
  R16 = Resistor [tolerance=±5% resistance=1M package="0805 [SMD]"]
  C9 = Ceramic Capacitor [capacitance=1nF voltage=16V part_number=3n9 package="1206 [SMD, multilayer]"]
  C10 = Ceramic Capacitor [capacitance="100 nF" voltage=16V package="1206 [SMD, multilayer]"]
  Input_Gain = Rotary Potentiometer (Small) [maximum_resistance=50k package=THT]
  R25 = Resistor [tolerance=±5% resistance=3.9k package="0805 [SMD]"]
  C11 = Ceramic Capacitor [capacitance="100 nF" voltage=16V package="1206 [SMD, multilayer]"]
  Mixer = Rotary Potentiometer (Small) [maximum_resistance=50k package=THT]
  R28 = Resistor Mini [tolerance=±5% resistance=1k package=THT]
  Feedback = Rotary Potentiometer (Small) [maximum_resistance=10kΩ package=THT]
  C12 = Ceramic Capacitor [capacitance="100 nF" voltage=16V package="1206 [SMD, multilayer]"]
  Output = AMPHENOL - ACJS-MHDR [package=ACJS-MHDR]
  Input = AMPHENOL - ACJS-MHDR [package=ACJS-MHDR]
  R31 = Resistor Mini [tolerance=±5% resistance=1k package=THT]
  R32 = Resistor [tolerance=±5% resistance=75k package="0805 [SMD]"]
  Atmega1285 = ATmega644 [package=pdpi]
  Power_5v = Power plug
  Y2 = CRYSTAL [package=hc49u-v]
  C28 = Ceramic Capacitor [capacitance=10pF voltage=50V part_number=27pF package="0603 [SMD, multilayer]"]
  C29 = Ceramic Capacitor [capacitance=10pF voltage=50V part_number=22pF package="0603 [SMD, multilayer]"]
  C31 = Ceramic Capacitor [capacitance=100nF voltage=50V part_number=100nF package="0603 [SMD, multilayer]"]
  R33 = Resistor Mini [tolerance=±5% resistance=10k package=THT]
  Up = Pushbutton [package="[THT]"]
  Dwn = Pushbutton [package="[THT]"]
  Effect = Pushbutton [package="[THT]"]
  Effect_On1 = LED - 3mm [color="Red (633nm)" package="3 mm [THT]"]
  R34 = Resistor [tolerance=±5% resistance=470 package="0603 [SMD]"]

nets:
  N1: U1.OUTA, C3.0, Input_Gain.leg2, Mixer.leg1
  N2: U1.-INA, R2.Pin_1, Input_Gain.leg1, Input_Gain.wiper
  N3: U1.+INA, R5.Pin_1, R28.Pin_1
  N4: U1.V+, R3.Pin_1, C11.1, Atmega1285.AVCC
  N5: U1.+INB, U1.+INC, R2.Pin_0, R3.Pin_0, C2.+, R5.Pin_0, R11.Pin_0
  N6: U1.-INB, R7.Pin_1, C5.1
  N7: U1.OUTB, R9.Pin_0, C5.0, R25.Pin_0
  N8: U1.OUTC, C7.0, R12.Pin_1, Mixer.leg2, Feedback.leg1
  N9: U1.-INC, C7.1, R13.Pin_1
  N10: U1.V-, C2.-, C4.0, C6.0, R11.Pin_1, C8.0, C9.1, C11.0, Feedback.leg2, Output.Sleeve_(1), Input.Sleeve_(1), Atmega1285.GND#30, C31.1, Up.Pin_1, Up.Pin_2, Dwn.Pin_1, Dwn.Pin_2, Effect.Pin_1, Effect.Pin_2
  N11: U1.+IND, Mixer.wiper
  N12: U1.-IND, U1.OUTD, R31.Pin_1
  N13: C1.0, R28.Pin_0
  N14: C1.1, Input.Tip_(6)
  N15: R7.Pin_0, R8.Pin_0, R9.Pin_1, C8.1, R32.Pin_1
  N16: R8.Pin_1, C3.1
  N17: C4.1, R12.Pin_0, R13.Pin_0, R14.Pin_1
  N18: C6.1, R25.Pin_1, Atmega1285.PA0
  N19: R14.Pin_0, R15.Pin_1, R16.Pin_1, C9.0
  N20: R15.Pin_0, Atmega1285.PD5
  N21: R16.Pin_0, Atmega1285.PD4
  N22: C10.0, R31.Pin_0
  N23: C10.1, Output.Tip_(3)
  N24: Feedback.wiper, C12.0
  N25: C12.1, R32.Pin_0
  N26: Atmega1285.PB0, R34.Pin_0
  N27: Atmega1285.PB1, Effect.Pin_3, Effect.Pin_4
  N28: Atmega1285.RESET, R33.Pin_0
  VCC: Atmega1285.VCC, Power_5v.VCC, R33.Pin_1, Effect_On1.cathode
  N29: Atmega1285.GND#10, Power_5v.GND, C28.0, C29.1
  N30: Atmega1285.XTAL2, Y2.1, C28.1
  N31: Atmega1285.XTAL1, Y2.2, C29.0
  N32: Atmega1285.AREF, C31.0
  N33: Atmega1285.PA5, Dwn.Pin_3, Dwn.Pin_4
  N34: Atmega1285.PA4, Up.Pin_3, Up.Pin_4
  N35: Effect_On1.anode, R34.Pin_1

custom parts:
  Resistor Mini: A generic resistor (0.25W)
